// Logisim project CPU Design.circ as structural Verilog: 15 circuits, main circuit AND
module AND (
  input  [4:0] A,
  input  [4:0] B,
  output [4:0] O
);

  and and_1 (O[0], A[0], B[0]);
  and and_2 (O[1], A[1], B[1]);
  and and_3 (O[2], A[2], B[2]);
  and and_4 (O[3], A[3], B[3]);
  and and_5 (O[4], A[4], B[4]);
endmodule

module SHL (
  input  [4:0] A,
  input  [2:0] Shift,
  output [4:0] O
);

  Multiplexer #(.select(3), .enable("false")) multiplexer_1 (
    .in0(A[4]), .in1(A[3]), .in2(A[2]), .in3(A[1]), .in4(A[0]), .in5(1'b0), .in6(1'b0), .in7(1'b0),
    .out(O[4]), .sel(Shift));
  Multiplexer #(.select(3), .enable("false")) multiplexer_2 (
    .in0(A[3]), .in1(A[2]), .in2(A[1]), .in3(A[0]), .in4(1'b0), .in5(1'b0), .in6(1'b0), .in7(1'b0),
    .out(O[3]), .sel(Shift));
  Multiplexer #(.select(3), .enable("false")) multiplexer_3 (
    .in0(A[2]), .in1(A[1]), .in2(A[0]), .in3(1'b0), .in4(1'b0), .in5(1'b0), .in6(1'b0), .in7(1'b0),
    .out(O[2]), .sel(Shift));
  Multiplexer #(.select(3), .enable("false")) multiplexer_4 (
    .in0(A[1]), .in1(A[0]), .in2(1'b0), .in3(1'b0), .in4(1'b0), .in5(1'b0), .in6(1'b0), .in7(1'b0),
    .out(O[1]), .sel(Shift));
  Multiplexer #(.select(3), .enable("false")) multiplexer_5 (
    .in0(A[0]), .in1(1'b0), .in2(1'b0), .in3(1'b0), .in4(1'b0), .in5(1'b0), .in6(1'b0), .in7(1'b0),
    .out(O[0]), .sel(Shift));
endmodule

// ZF
module ALU (
  input  [4:0] A,
  input  [4:0] B,
  input  OP,
  output CF,
  output [4:0] O,
  output SF,
  output ZF
);

  wire or_1_out;
  wire [4:0] AND, SHL;

  AND and_1 (.A(A), .B(B), .O(AND));
  SHL shl_1 (.A(A), .Shift(B[2:0]), .O(SHL));
  Multiplexer #(.width(5), .enable("false")) multiplexer_1 (.in0(AND), .in1(SHL), .out(O), .sel(OP));
  or or_1 (or_1_out, O[0], O[1], O[2], O[3], O[4]);
  not not_1 (ZF, or_1_out);

  assign CF = 1'b1;
  assign SF = O[4];

  // Notes on the sheet:
  //   Let's assume we have always a carry for JC
endmodule

module test (
  input  [17:0] Write_Data_17_0,
  input  in_2,
  input  in_3,
  input  in_4,
  input  in_5,
  output [17:0] Read_Data_1,
  output [17:0] Read_Data_2
);

  _1X18_SRAM u_1x18_sram_1 (
    .Write_Data_17_0(Write_Data_17_0), .Write_Select(in_2), .Read_Select_1(in_3), .Read_Select_2(in_4),
    .Clock(in_5), .Read_Data_1(Read_Data_1), .Read_Data_2(Read_Data_2));
endmodule

module _1_bit_Register (
  input  Din,
  input  Sel,
  input  Clock,
  output Dout
);

  wire multiplexer_1_out;

  Multiplexer #(.enable("false")) multiplexer_1 (.in0(Dout), .in1(Din), .out(multiplexer_1_out), .sel(Sel));
  D_Flip_Flop d_ff_1 (.clk(Clock), .D(multiplexer_1_out), .Q(Dout));  // open: Qn, preset, en, reset
endmodule

module _5_bit_Register (
  input  [4:0] Din_4_0,
  input  Sel,
  input  Clk,
  output [4:0] Dout_4_0
);

  _1_bit_Register u_1_bit_register_1 (.Din(Din_4_0[0]), .Sel(Sel), .Dout(Dout_4_0[0]), .Clock(Clk));
  _1_bit_Register u_1_bit_register_2 (.Din(Din_4_0[1]), .Sel(Sel), .Dout(Dout_4_0[1]), .Clock(Clk));
  _1_bit_Register u_1_bit_register_3 (.Din(Din_4_0[2]), .Sel(Sel), .Dout(Dout_4_0[2]), .Clock(Clk));
  _1_bit_Register u_1_bit_register_4 (.Din(Din_4_0[3]), .Sel(Sel), .Dout(Dout_4_0[3]), .Clock(Clk));
  _1_bit_Register u_1_bit_register_5 (.Din(Din_4_0[4]), .Sel(Sel), .Dout(Dout_4_0[4]), .Clock(Clk));
endmodule

module Register_Set (
  input  [4:0] WRD,
  input  WE,
  input  [1:0] WR,
  input  [1:0] RA,
  input  [1:0] RB,
  input  CLK,
  output [4:0] A,
  output [4:0] B
);

  wire decoder_1_out0, decoder_1_out1, decoder_1_out2, decoder_1_out3;
  wire [4:0] R0, R1, R2, R3;

  Decoder #(.select(2)) decoder_1 (
    .out0(decoder_1_out0), .out1(decoder_1_out1), .out2(decoder_1_out2), .out3(decoder_1_out3), .sel(WR),
    .en(WE));
  _5_bit_Register u_5_bit_register_1 (.Din_4_0(WRD), .Sel(decoder_1_out0), .Dout_4_0(R0), .Clk(CLK));
  _5_bit_Register u_5_bit_register_2 (.Din_4_0(WRD), .Sel(decoder_1_out1), .Dout_4_0(R1), .Clk(CLK));
  _5_bit_Register u_5_bit_register_3 (.Din_4_0(WRD), .Sel(decoder_1_out2), .Dout_4_0(R2), .Clk(CLK));
  _5_bit_Register u_5_bit_register_4 (.Din_4_0(WRD), .Sel(decoder_1_out3), .Dout_4_0(R3), .Clk(CLK));
  Multiplexer #(.select(2), .width(5), .enable("false")) multiplexer_1 (
    .in0(R0), .in1(R1), .in2(R2), .in3(R3), .out(A), .sel(RA));
  Multiplexer #(.select(2), .width(5), .enable("false")) multiplexer_2 (
    .in0(R0), .in1(R1), .in2(R2), .in3(R3), .out(B), .sel(RB));
endmodule

module _1x1_SRAM (
  input  Read_Select_1,
  input  Read_Select_1_2,
  input  Write_Data,
  input  Write_Sel,
  input  Clock,
  output Read_Data_1,
  output Read_Data_2
);

  wire d_ff_1_q, multiplexer_1_out;

  Multiplexer #(.enable("false")) multiplexer_1 (
    .in0(d_ff_1_q), .in1(Write_Data), .out(multiplexer_1_out), .sel(Write_Sel));
  D_Flip_Flop d_ff_1 (.clk(Clock), .D(multiplexer_1_out), .Q(d_ff_1_q));  // open: Qn, preset, en, reset
  and and_1 (Read_Data_1, Read_Select_1, d_ff_1_q);
  and and_2 (Read_Data_2, Read_Select_1_2, d_ff_1_q);
endmodule

module _1X18_SRAM (
  input  [17:0] Write_Data_17_0,
  input  Write_Select,
  input  Read_Select_1,
  input  Read_Select_2,
  input  Clock,
  output [17:0] Read_Data_1,
  output [17:0] Read_Data_2
);

  _1x1_SRAM u_1x1_sram_1 (
    .Read_Select_1(Read_Select_1), .Read_Select_1_2(Read_Select_2), .Write_Data(Write_Data_17_0[0]),
    .Write_Sel(Write_Select), .Clock(Clock), .Read_Data_1(Read_Data_1[0]), .Read_Data_2(Read_Data_2[0]));
  _1x1_SRAM u_1x1_sram_2 (
    .Read_Select_1(Read_Select_1), .Read_Select_1_2(Read_Select_2), .Write_Data(Write_Data_17_0[6]),
    .Write_Sel(Write_Select), .Clock(Clock), .Read_Data_1(Read_Data_1[6]), .Read_Data_2(Read_Data_2[6]));
  _1x1_SRAM u_1x1_sram_3 (
    .Read_Select_1(Read_Select_1), .Read_Select_1_2(Read_Select_2), .Write_Data(Write_Data_17_0[12]),
    .Write_Sel(Write_Select), .Clock(Clock), .Read_Data_1(Read_Data_1[12]), .Read_Data_2(Read_Data_2[12]));
  _1x1_SRAM u_1x1_sram_4 (
    .Read_Select_1(Read_Select_1), .Read_Select_1_2(Read_Select_2), .Write_Data(Write_Data_17_0[1]),
    .Write_Sel(Write_Select), .Clock(Clock), .Read_Data_1(Read_Data_1[1]), .Read_Data_2(Read_Data_2[1]));
  _1x1_SRAM u_1x1_sram_5 (
    .Read_Select_1(Read_Select_1), .Read_Select_1_2(Read_Select_2), .Write_Data(Write_Data_17_0[7]),
    .Write_Sel(Write_Select), .Clock(Clock), .Read_Data_1(Read_Data_1[7]), .Read_Data_2(Read_Data_2[7]));
  _1x1_SRAM u_1x1_sram_6 (
    .Read_Select_1(Read_Select_1), .Read_Select_1_2(Read_Select_2), .Write_Data(Write_Data_17_0[13]),
    .Write_Sel(Write_Select), .Clock(Clock), .Read_Data_1(Read_Data_1[13]), .Read_Data_2(Read_Data_2[13]));
  _1x1_SRAM u_1x1_sram_7 (
    .Read_Select_1(Read_Select_1), .Read_Select_1_2(Read_Select_2), .Write_Data(Write_Data_17_0[2]),
    .Write_Sel(Write_Select), .Clock(Clock), .Read_Data_1(Read_Data_1[2]), .Read_Data_2(Read_Data_2[2]));
  _1x1_SRAM u_1x1_sram_8 (
    .Read_Select_1(Read_Select_1), .Read_Select_1_2(Read_Select_2), .Write_Data(Write_Data_17_0[8]),
    .Write_Sel(Write_Select), .Clock(Clock), .Read_Data_1(Read_Data_1[8]), .Read_Data_2(Read_Data_2[8]));
  _1x1_SRAM u_1x1_sram_9 (
    .Read_Select_1(Read_Select_1), .Read_Select_1_2(Read_Select_2), .Write_Data(Write_Data_17_0[14]),
    .Write_Sel(Write_Select), .Clock(Clock), .Read_Data_1(Read_Data_1[14]), .Read_Data_2(Read_Data_2[14]));
  _1x1_SRAM u_1x1_sram_10 (
    .Read_Select_1(Read_Select_1), .Read_Select_1_2(Read_Select_2), .Write_Data(Write_Data_17_0[3]),
    .Write_Sel(Write_Select), .Clock(Clock), .Read_Data_1(Read_Data_1[3]), .Read_Data_2(Read_Data_2[3]));
  _1x1_SRAM u_1x1_sram_11 (
    .Read_Select_1(Read_Select_1), .Read_Select_1_2(Read_Select_2), .Write_Data(Write_Data_17_0[9]),
    .Write_Sel(Write_Select), .Clock(Clock), .Read_Data_1(Read_Data_1[9]), .Read_Data_2(Read_Data_2[9]));
  _1x1_SRAM u_1x1_sram_12 (
    .Read_Select_1(Read_Select_1), .Read_Select_1_2(Read_Select_2), .Write_Data(Write_Data_17_0[15]),
    .Write_Sel(Write_Select), .Clock(Clock), .Read_Data_1(Read_Data_1[15]), .Read_Data_2(Read_Data_2[15]));
  _1x1_SRAM u_1x1_sram_13 (
    .Read_Select_1(Read_Select_1), .Read_Select_1_2(Read_Select_2), .Write_Data(Write_Data_17_0[4]),
    .Write_Sel(Write_Select), .Clock(Clock), .Read_Data_1(Read_Data_1[4]), .Read_Data_2(Read_Data_2[4]));
  _1x1_SRAM u_1x1_sram_14 (
    .Read_Select_1(Read_Select_1), .Read_Select_1_2(Read_Select_2), .Write_Data(Write_Data_17_0[10]),
    .Write_Sel(Write_Select), .Clock(Clock), .Read_Data_1(Read_Data_1[10]), .Read_Data_2(Read_Data_2[10]));
  _1x1_SRAM u_1x1_sram_15 (
    .Read_Select_1(Read_Select_1), .Read_Select_1_2(Read_Select_2), .Write_Data(Write_Data_17_0[16]),
    .Write_Sel(Write_Select), .Clock(Clock), .Read_Data_1(Read_Data_1[16]), .Read_Data_2(Read_Data_2[16]));
  _1x1_SRAM u_1x1_sram_16 (
    .Read_Select_1(Read_Select_1), .Read_Select_1_2(Read_Select_2), .Write_Data(Write_Data_17_0[5]),
    .Write_Sel(Write_Select), .Clock(Clock), .Read_Data_1(Read_Data_1[5]), .Read_Data_2(Read_Data_2[5]));
  _1x1_SRAM u_1x1_sram_17 (
    .Read_Select_1(Read_Select_1), .Read_Select_1_2(Read_Select_2), .Write_Data(Write_Data_17_0[11]),
    .Write_Sel(Write_Select), .Clock(Clock), .Read_Data_1(Read_Data_1[11]), .Read_Data_2(Read_Data_2[11]));
  _1x1_SRAM u_1x1_sram_18 (
    .Read_Select_1(Read_Select_1), .Read_Select_1_2(Read_Select_2), .Write_Data(Write_Data_17_0[17]),
    .Write_Sel(Write_Select), .Clock(Clock), .Read_Data_1(Read_Data_1[17]), .Read_Data_2(Read_Data_2[17]));

  // Other names for the same wires on the sheet: CLK = Clock; RD1_0 = Read_Data_1[0]; RD1_1 = Read_Data_1[1];
  //   RD1_2 = Read_Data_1[2]; RD1_3 = Read_Data_1[3]; RD1_4 = Read_Data_1[4]; RD1_5 = Read_Data_1[5];
  //   RD1_6 = Read_Data_1[6]; RD1_7 = Read_Data_1[7]; RD1_8 = Read_Data_1[8]; RD1_9 = Read_Data_1[9];
  //   RD1_10 = Read_Data_1[10]; RD1_11 = Read_Data_1[11]; RD1_12 = Read_Data_1[12]; RD1_13 = Read_Data_1[13];
  //   RD1_14 = Read_Data_1[14]; RD1_15 = Read_Data_1[15]; RD1_16 = Read_Data_1[16]; RD1_17 = Read_Data_1[17];
  //   RD2_0 = Read_Data_2[0]; RD2_1 = Read_Data_2[1]; RD2_2 = Read_Data_2[2]; RD2_3 = Read_Data_2[3];
  //   RD2_4 = Read_Data_2[4]; RD2_5 = Read_Data_2[5]; RD2_6 = Read_Data_2[6]; RD2_7 = Read_Data_2[7];
  //   RD2_8 = Read_Data_2[8]; RD2_9 = Read_Data_2[9]; RD2_10 = Read_Data_2[10]; RD2_11 = Read_Data_2[11];
  //   RD2_12 = Read_Data_2[12]; RD2_13 = Read_Data_2[13]; RD2_14 = Read_Data_2[14]; RD2_15 = Read_Data_2[15];
  //   RD2_16 = Read_Data_2[16]; RD2_17 = Read_Data_2[17]; RS1 = Read_Select_1; RS2 = Read_Select_2;
  //   D0 = Write_Data_17_0[0]; D1 = Write_Data_17_0[1]; D2 = Write_Data_17_0[2]; D3 = Write_Data_17_0[3];
  //   D4 = Write_Data_17_0[4]; D5 = Write_Data_17_0[5]; D6 = Write_Data_17_0[6]; D7 = Write_Data_17_0[7];
  //   D8 = Write_Data_17_0[8]; D9 = Write_Data_17_0[9]; D10 = Write_Data_17_0[10]; D11 = Write_Data_17_0[11];
  //   D12 = Write_Data_17_0[12]; D13 = Write_Data_17_0[13]; D14 = Write_Data_17_0[14]; D15 = Write_Data_17_0[15];
  //   D16 = Write_Data_17_0[16]; D17 = Write_Data_17_0[17]; WS = Write_Select
endmodule

module _10x18_SRAM (
  input  [17:0] Write_Data_17_0,
  input  [3:0] Read_Address_1__3_0,
  input  [3:0] Read_Address_2__3_0,
  input  Write_Enable,
  input  [3:0] Write_Address__3_0,
  input  CLK,
  output [17:0] Read_Data_1_17_0,
  output [17:0] Read_Data_2
);

  wire R1_0, R1_1, R1_2, R1_3, R1_4, R1_5, R1_6, R1_7, R1_8, R1_9, R2_0, R2_1, R2_2, R2_3, R2_4, R2_5, R2_6,
       R2_7, R2_8, R2_9, W0, W1, W2, W3, W4, W5, W6, W7, W8, W9;
  wire [17:0] RD1_0, RD1_1, RD1_2, RD1_3, RD1_4, RD1_5, RD1_6, RD1_7, RD1_8, RD1_9, RD2_0, RD2_1, RD2_2,
       RD2_3, RD2_4, RD2_5, RD2_6, RD2_7, RD2_8, RD2_9;

  Decoder #(.select(4), .enable("false")) decoder_1 (
    .out0(R1_0), .out1(R1_1), .out2(R1_2), .out3(R1_3), .out4(R1_4), .out5(R1_5), .out6(R1_6), .out7(R1_7),
    .out8(R1_8), .out9(R1_9), .sel(Read_Address_1__3_0));  // open: out10, out11, out12, out13, out14, out15
  Decoder #(.select(4), .enable("false")) decoder_2 (
    .out0(R2_0), .out1(R2_1), .out2(R2_2), .out3(R2_3), .out4(R2_4), .out5(R2_5), .out6(R2_6), .out7(R2_7),
    .out8(R2_8), .out9(R2_9), .sel(Read_Address_2__3_0));  // open: out10, out11, out12, out13, out14, out15
  Decoder #(.select(4)) decoder_3 (
    .out0(W0), .out1(W1), .out2(W2), .out3(W3), .out4(W4), .out5(W5), .out6(W6), .out7(W7), .out8(W8),
    .out9(W9), .sel(Write_Address__3_0), .en(Write_Enable));  // open: out10, out11, out12, out13, out14, out15
  _1X18_SRAM u_1x18_sram_1 (
    .Write_Data_17_0(Write_Data_17_0), .Write_Select(W0), .Read_Select_1(R1_0), .Read_Select_2(R2_0),
    .Clock(CLK), .Read_Data_1(RD1_0), .Read_Data_2(RD2_0));
  _1X18_SRAM u_1x18_sram_2 (
    .Write_Data_17_0(Write_Data_17_0), .Write_Select(W1), .Read_Select_1(R1_1), .Read_Select_2(R2_1),
    .Clock(CLK), .Read_Data_1(RD1_1), .Read_Data_2(RD2_1));
  _1X18_SRAM u_1x18_sram_3 (
    .Write_Data_17_0(Write_Data_17_0), .Write_Select(W2), .Read_Select_1(R1_2), .Read_Select_2(R2_2),
    .Clock(CLK), .Read_Data_1(RD1_2), .Read_Data_2(RD2_2));
  _1X18_SRAM u_1x18_sram_4 (
    .Write_Data_17_0(Write_Data_17_0), .Write_Select(W3), .Read_Select_1(R1_3), .Read_Select_2(R2_3),
    .Clock(CLK), .Read_Data_1(RD1_3), .Read_Data_2(RD2_3));
  _1X18_SRAM u_1x18_sram_5 (
    .Write_Data_17_0(Write_Data_17_0), .Write_Select(W4), .Read_Select_1(R1_4), .Read_Select_2(R2_4),
    .Clock(CLK), .Read_Data_1(RD1_4), .Read_Data_2(RD2_4));
  _1X18_SRAM u_1x18_sram_6 (
    .Write_Data_17_0(Write_Data_17_0), .Write_Select(W5), .Read_Select_1(R1_5), .Read_Select_2(R2_5),
    .Clock(CLK), .Read_Data_1(RD1_5), .Read_Data_2(RD2_5));
  _1X18_SRAM u_1x18_sram_7 (
    .Write_Data_17_0(Write_Data_17_0), .Write_Select(W6), .Read_Select_1(R1_6), .Read_Select_2(R2_6),
    .Clock(CLK), .Read_Data_1(RD1_6), .Read_Data_2(RD2_6));
  _1X18_SRAM u_1x18_sram_8 (
    .Write_Data_17_0(Write_Data_17_0), .Write_Select(W7), .Read_Select_1(R1_7), .Read_Select_2(R2_7),
    .Clock(CLK), .Read_Data_1(RD1_7), .Read_Data_2(RD2_7));
  _1X18_SRAM u_1x18_sram_9 (
    .Write_Data_17_0(Write_Data_17_0), .Write_Select(W8), .Read_Select_1(R1_8), .Read_Select_2(R2_8),
    .Clock(CLK), .Read_Data_1(RD1_8), .Read_Data_2(RD2_8));
  _1X18_SRAM u_1x18_sram_10 (
    .Write_Data_17_0(Write_Data_17_0), .Write_Select(W9), .Read_Select_1(R1_9), .Read_Select_2(R2_9),
    .Clock(CLK), .Read_Data_1(RD1_9), .Read_Data_2(RD2_9));
  assign Read_Data_1_17_0 = RD1_0 | RD1_1 | RD1_2 | RD1_3 | RD1_4 | RD1_5 | RD1_6 | RD1_7 | RD1_8 | RD1_9;  // OR_Gate or_1, 18 bits wide
  assign Read_Data_2 = RD2_0 | RD2_1 | RD2_2 | RD2_3 | RD2_4 | RD2_5 | RD2_6 | RD2_7 | RD2_8 | RD2_9;  // OR_Gate or_2, 18 bits wide
endmodule

module CPU (
  input  [3:0] Write_Address__3_0,
  input  Write_Enable,
  input  [17:0] Write_Data_17_0,
  input  Clock,
  input  CPU_Enable
);

  wire alu_1_cf, alu_1_sf, alu_1_zf, CF, CPU_CLK, Imm_Sel, Jmp_Sel, OP, WE;
  wire [3:0] JMP_Addr, multiplexer_1_out, n4_bit_counter_register_1_dout_3_0, n4_bit_pc_adder_1_o_3_0;
  wire [4:0] alu_1_o, multiplexer_2_out, register_set_1_a, register_set_1_b;
  wire [17:0] n10x18_sram_1_read_data_1_17_0;

  _4_Bit_PC_Adder u_4_bit_pc_adder_1 (.I_3_0(n4_bit_counter_register_1_dout_3_0), .O_3_0(n4_bit_pc_adder_1_o_3_0));
  Multiplexer #(.width(4), .enable("false")) multiplexer_1 (
    .in0(n4_bit_pc_adder_1_o_3_0), .in1(JMP_Addr), .out(multiplexer_1_out), .sel(Jmp_Sel));
  and and_1 (CPU_CLK, Clock, CPU_Enable);
  _4_Bit_Counter_Register u_4_bit_counter_register_1 (
    .Din_3_0(multiplexer_1_out), .Clk(CPU_CLK), .Dout_3_0(n4_bit_counter_register_1_dout_3_0));
  _10x18_SRAM u_10x18_sram_1 (
    .Write_Data_17_0(Write_Data_17_0), .Read_Address_1__3_0(n4_bit_counter_register_1_dout_3_0),
    .Write_Enable(Write_Enable), .Write_Address__3_0(Write_Address__3_0), .CLK(Clock),
    .Read_Data_1_17_0({n10x18_sram_1_read_data_1_17_0[17:15], JMP_Addr, n10x18_sram_1_read_data_1_17_0[10:0]}));  // open: Read_Address_2__3_0, Read_Data_2
  Control_Unit control_unit_1 (
    .Opcode_2_0(n10x18_sram_1_read_data_1_17_0[17:15]), .Op_1_0(OP), .Imm_Sel(Imm_Sel), .WE(WE), .CF(CF),
    .Jmp_Sel(Jmp_Sel));
  Register_Set register_set_1 (
    .WRD(alu_1_o), .WE(WE), .WR(JMP_Addr[3:2]), .RA(JMP_Addr[3:2]), .RB(JMP_Addr[1:0]), .A(register_set_1_a),
    .B(register_set_1_b), .CLK(CPU_CLK));
  Multiplexer #(.width(5), .enable("false")) multiplexer_2 (
    .in0(register_set_1_b), .in1({JMP_Addr[1:0], n10x18_sram_1_read_data_1_17_0[10:8]}),
    .out(multiplexer_2_out), .sel(Imm_Sel));
  Flag_Register flag_register_1 (
    .ZFin(alu_1_zf), .CFin(alu_1_cf), .SFin(alu_1_sf), .Clk(Clock), .CFout(CF));  // open: ZFout, SFout
  ALU alu_1 (
    .A(register_set_1_a), .B(multiplexer_2_out), .OP(OP), .O(alu_1_o), .CF(alu_1_cf), .SF(alu_1_sf),
    .ZF(alu_1_zf));

  // Other names for the same wires on the sheet: CLK = Clock
endmodule

module _4_Bit_Counter_Register (
  input  [3:0] Din_3_0,
  input  Clk,
  output [3:0] Dout_3_0
);

  _1_bit_Register u_1_bit_register_1 (.Din(Din_3_0[0]), .Sel(1'b1), .Dout(Dout_3_0[0]), .Clock(Clk));
  _1_bit_Register u_1_bit_register_2 (.Din(Din_3_0[1]), .Sel(1'b1), .Dout(Dout_3_0[1]), .Clock(Clk));
  _1_bit_Register u_1_bit_register_3 (.Din(Din_3_0[2]), .Sel(1'b1), .Dout(Dout_3_0[2]), .Clock(Clk));
  _1_bit_Register u_1_bit_register_4 (.Din(Din_3_0[3]), .Sel(1'b1), .Dout(Dout_3_0[3]), .Clock(Clk));
endmodule

module _4_Bit_PC_Adder (
  input  [3:0] I_3_0,
  output [3:0] O_3_0
);

  wire [3:0] bit_extender_1_out;

  assign bit_extender_1_out = {{3{1'b0}}, 1'b1};  // Bit_Extender bit_extender_1
  Adder #(.width(4)) adder_1 (.a(I_3_0), .b(bit_extender_1_out), .out(O_3_0));  // open: cin, cout
endmodule

module Control_Unit (
  input  [2:0] Opcode_2_0,
  input  CF,
  output Op_1_0,
  output Imm_Sel,
  output WE,
  output Jmp_Sel
);

  wire Brch_out, not_1_out, not_2_out, not_3_out, not_4_out, Reg_out;

  not not_1 (not_1_out, Opcode_2_0[2]);
  not not_2 (not_2_out, Opcode_2_0[2]);
  not not_3 (not_3_out, Opcode_2_0[1]);
  not not_4 (not_4_out, Opcode_2_0[1]);
  and Imm (Imm_Sel, not_1_out, Opcode_2_0[1]);
  and Reg (Reg_out, not_2_out, not_3_out);
  and Brch (Brch_out, Opcode_2_0[2], not_4_out);
  or or_1 (WE, Imm_Sel, Reg_out);
  and and_1 (Jmp_Sel, Brch_out, CF);

  assign Op_1_0 = Opcode_2_0[0];
endmodule

module Flag_Register (
  input  ZFin,
  input  CFin,
  input  SFin,
  input  Clk,
  output ZFout,
  output CFout,
  output SFout
);

  _1_bit_Register u_1_bit_register_1 (.Din(ZFin), .Sel(1'b1), .Dout(ZFout), .Clock(Clk));
  _1_bit_Register u_1_bit_register_2 (.Din(CFin), .Sel(1'b1), .Dout(CFout), .Clock(Clk));
  _1_bit_Register u_1_bit_register_3 (.Din(SFin), .Sel(1'b1), .Dout(SFout), .Clock(Clk));
endmodule
